# Fritzing sketch TCC_MÓDULO SD (saved by Fritzing 0.9.3b)

parts:
  SD_card_module1 = SD Card Module
  Componente1 = Arduino Mega 2560 (Rev3)

nets:
  N1: SD_card_module1.+5, Componente1.5V
  N2: SD_card_module1.CS, Componente1.D53
  N3: SD_card_module1.MOSI, Componente1.D51
  N4: SD_card_module1.SCK, Componente1.D52
  N5: SD_card_module1.MISO, Componente1.D50
  GND: SD_card_module1.GND, Componente1.GND

custom parts:
  SD Card Module: SD Card Module Slot Socket Reader For Arduino ARM MCU
