# Fritzing sketch TCC_rele (saved by Fritzing 0.9.3b)
breadboards: 1

parts:
  Componente1 = Arduino Mega 2560 (Rev3)
  U1 = 4-Channel 5v Relay Shield [package=relay-4ch5v10a]
  U2 = 4-Channel 5v Relay Shield [package=relay-4ch5v10a]
  VCC1 = 4 x AAA Battery Mount
  M1 = DC Motor
  M2 = DC Motor
  M3 = DC Motor
  M4 = DC Motor

nets:
  N1: Componente1.D12_PWM, U2.IN1
  N2: Componente1.D11_PWM, U2.IN3
  N3: Componente1.D10_PWM, U1.IN1
  N4: Componente1.D9_PWM, U1.IN3
  N5: Componente1.D8_PWM, U2.IN2
  VCC: Componente1.5V, U1.VCC, U2.VCC
  GND: Componente1.GND, U1.GND, U2.GND
  N6: Componente1.D5_PWM, U1.IN4
  N7: Componente1.D6_PWM, U1.IN2
  N8: Componente1.D7_PWM, U2.IN4
  N9: U1.K1-In, U1.K2-In, U1.K3-In, U1.K4-In, U2.K1-In, U2.K2-In, U2.K3-In, U2.K4-In, VCC1.+
  N10: U1.K1-Off, M4.pin_1
  N11: U1.K1-On, U1.K2-On, U1.K3-On, U1.K4-On, U2.K1-On, U2.K2-On, U2.K3-On, U2.K4-On, VCC1.-
  N12: U1.K2-Off, M4.pin_2
  N13: U1.K3-Off, M3.pin_1
  N14: U1.K4-Off, M3.pin_2
  N15: U2.K1-Off, M1.pin_1
  N16: U2.K2-Off, M1.pin_2
  N17: U2.K3-Off, M2.pin_1
  N18: U2.K4-Off, M2.pin_2

custom parts:
  4-Channel 5v Relay Shield: 4 Channel 5v Relay Shield w. 2x SPD-06VDC-SD-C
