# Fritzing sketch TCC_sensor (saved by Fritzing 0.9.3b)

parts:
  Componente1 = Arduino Mega 2560 (Rev3)
  J1 = Infrared Proximity Sensor

nets:
  GND: Componente1.GND, J1.GND
  N1: Componente1.D4_PWM, J1.Vout
  5V: Componente1.5V, J1.Vcc
